# Fritzing sketch Untitled Sketch 2 (saved by Fritzing 0.9.3b)
breadboards: 1

parts:
  M2 = fc-51 [package=THT]
  M3 = fc-51 [package=THT]
  S1 = Round Pushbutton
  A2 = WS2811-LED-strip_1
  Conductivity_Circuit1 = Conductivity Circuit  # not connected
  WeMos_D1_Mini1 = WeMos D1 Mini
  A4 = WS2811-LED-strip_1

nets:
  N1: M2.pin1, WeMos_D1_Mini1.D4
  N2: M2.pin2, M3.pin2, S1.leg1, A2.connector3, WeMos_D1_Mini1.G, A4.connector3
  N3: M2.pin3, M3.pin3, A2.connector5, WeMos_D1_Mini1.5V, A4.connector5
  N4: M3.pin1, WeMos_D1_Mini1.D5
  N5: S1.leg0, WeMos_D1_Mini1.D2
  N6: A2.connector4, WeMos_D1_Mini1.D7
  N7: WeMos_D1_Mini1.D6, A4.connector4
